// Logisim project MUO.circ as structural Verilog: 12 circuits, main circuit CPU
module CPU (
  input  in_1,
  input  Clear,
  output [11:0] PC,
  output [15:0] IR,
  output [15:0] ACC,
  output [15:0] ALU,
  output [15:0] OR,
  output [11:0] Address_Bus,
  output [15:0] Data_Bus
);

  wire ACCr, ACCw, ALUs0, ALUs1, clock, clock_1_out, HLT, IRw, MEMr, MEMw, MuxA, MuxB, N, not_1_out,
       not_2_out, P, PCw, Z;
  wire [3:0] ir_1_opcode;
  wire [11:0] alu_1_aout, ir_1_address, pc_1_pc_out;
  wire [15:0] acc_1_dout, alu_1_dout, bit_extender_1_out, multiplexer_1_out, ram_1_data;

  assign bit_extender_1_out = {{4{1'b0}}, Address_Bus};  // Bit_Extender bit_extender_1
  Multiplexer #(.width(16), .enable("false")) multiplexer_1 (
    .in0(bit_extender_1_out), .in1(Data_Bus), .out(multiplexer_1_out), .sel(MuxB));
  ACC acc_1 (
    .in_3(alu_1_dout), .Dout(acc_1_dout), .ACCw(ACCw), .Clock(clock), .clear(Clear), .debug(ACC),
    .zero_flag(Z), .neg_flag(N), .pos_flag(P));
  assign Data_Bus = ACCr ? acc_1_dout : 16'bz;  // Controlled_Buffer controlled_buffer_1
  ALU alu_1 (
    .A(acc_1_dout), .B(multiplexer_1_out), .Dout(alu_1_dout), .Aout(alu_1_aout), .debug(ALU), .Alu0(ALUs0),
    .Alu1(ALUs1));
  PC pc_1 (.PC_in(alu_1_aout), .PC_out(pc_1_pc_out), .clock(clock), .PCw(PCw), .clear(Clear), .debug(PC));
  Multiplexer #(.width(12), .enable("false")) multiplexer_2 (
    .in0(pc_1_pc_out), .in1(ir_1_address), .out(Address_Bus), .sel(MuxA));
  IR ir_1 (
    .in_3(Data_Bus), .IRw(IRw), .Clock(clock), .clear(Clear), .debug(IR), .Address(ir_1_address),
    .OPcode(ir_1_opcode));
  OR or_1 (.Din(Data_Bus), .Dout(OR), .ORw(in_1), .Clock(clock), .clear(Clear));
  CCU ccu_1 (
    .clock(clock), .clear(Clear), .MEMw(MEMw), .MEMr(MEMr), .PCw(PCw), .IRw(IRw), .MuxA(MuxA), .MuxB(MuxB),
    .ACCw(ACCw), .ACCr(ACCr), .ALUs1(ALUs1), .ALUs0(ALUs0), .OPcode(ir_1_opcode), .Neg_flag(N),
    .zero_flag(Z), .pos_flag(P), .HALT(HLT));
  not not_1 (not_1_out, MEMr);
  assign Data_Bus = ~MEMw ? ram_1_data : 16'bz;  // Controlled_Buffer controlled_buffer_2
  assign clock = not_2_out ? clock_1_out : 1'bz;  // Controlled_Buffer controlled_buffer_3
  not not_2 (not_2_out, HLT);
  Clock clock_1 (.out(clock_1_out));
  RAM #(.addrWidth(12), .dataWidth(16), .bus("separate"), .simpleMode("false"), .Select("low")) ram_1 (
    .addr(Address_Bus), .din(Data_Bus), .data(ram_1_data), .str(MEMw), .sel(not_1_out), .clk(clock));  // open: ld, clr

  // Other names for the same wires on the sheet: AB[11:0] = Address_Bus; DB[15:0] = Data_Bus; ORw = in_1

  // Notes on the sheet:
  //   ADDRESS BUS
  //   DATA BUS
endmodule

module PC (
  input  clock,
  input  PCw,
  input  [11:0] PC_in,
  input  clear,
  output [11:0] PC_out,
  output [11:0] debug
);

  register_12bits register_12bits_1 (
    .Data_in(PC_in), .Clock(clock), .Write(PCw), .clear(clear), .Data_out(PC_out), .Data_stored(debug),
    .Read(1'b1));
endmodule

module IR (
  input  IRw,
  input  Clock,
  input  [15:0] in_3,
  input  clear,
  output [11:0] Address,
  output [3:0] OPcode,
  output [15:0] debug
);

  register_16bits register_16bits_1 (
    .Din(in_3), .Dout({OPcode, Address}), .W(IRw), .Clock(Clock), .Clear(clear), .debug(debug), .OE(1'b1));
endmodule

module ALU (
  input  Alu1,
  input  Alu0,
  input  [15:0] B,
  input  [15:0] A,
  output [11:0] Aout,
  output [15:0] Dout,
  output [15:0] debug
);

  wire and_1_out, xor_1_out;
  wire [15:0] adder_1_out, multiplexer_1_out, multiplexer_2_out, not_1_out;

  assign not_1_out = ~B;  // NOT_Gate not_1, 16 bits wide
  xor xor_1 (xor_1_out, and_1_out, Alu0);
  Multiplexer #(.width(16), .enable("false")) multiplexer_1 (
    .in0(B), .in1(not_1_out), .out(multiplexer_1_out), .sel(xor_1_out));
  Multiplexer #(.width(16), .enable("false")) multiplexer_2 (
    .in0(A), .in1({16{1'b0}}), .out(multiplexer_2_out), .sel(and_1_out));
  and and_1 (and_1_out, Alu1, Alu0);
  Adder #(.width(16)) adder_1 (
    .a(multiplexer_1_out), .b(multiplexer_2_out), .out(adder_1_out), .cin(Alu0));  // open: cout
  Multiplexer #(.select(2), .width(16), .enable("false")) multiplexer_3 (
    .in0(multiplexer_1_out), .in1(adder_1_out), .in2(adder_1_out), .in3(adder_1_out),
    .out({debug[15:12], Aout}), .sel({Alu1, Alu0}));

  assign debug[11:0] = Aout;
  assign Dout = {debug[15:12], Aout};
endmodule

module ACC (
  input  ACCw,
  input  Clock,
  input  [15:0] in_3,
  input  clear,
  output [15:0] Dout,
  output [15:0] debug,
  output zero_flag,
  output neg_flag,
  output pos_flag
);

  wire not_1_out;

  register_16bits register_16bits_1 (
    .Din(in_3), .Dout(Dout), .W(ACCw), .Clock(Clock), .Clear(clear), .debug(debug), .OE(1'b1));
  nor nor_1 (zero_flag, Dout[0], Dout[1], Dout[2], Dout[3], Dout[4], Dout[5], Dout[6], Dout[7], Dout[8], Dout[9], Dout[10], Dout[11], Dout[12], Dout[13], Dout[14], Dout[15]);
  not not_1 (not_1_out, Dout[15]);
  xor xor_1 (pos_flag, not_1_out, zero_flag);

  assign neg_flag = Dout[15];
endmodule

module CAR (
  input  clk,
  input  Write,
  input  [4:0] \input ,
  input  clear,
  output [4:0] \output 
);

  wire not_1_out;

  Counter #(.width(5), .max('h1f), .behavior("old")) counter_1 (
    .load(Write), .D(\input ), .count(not_1_out), .Q(\output ), .clk(clk), .clr(clear));  // open: carry, preset
  not not_1 (not_1_out, Write);
endmodule

module CCU (
  input  clear,
  input  clock,
  input  Neg_flag,
  input  zero_flag,
  input  pos_flag,
  input  [3:0] OPcode,
  output MEMw,
  output ACCw,
  output ALUs1,
  output MEMr,
  output IRw,
  output MuxB,
  output ACCr,
  output ALUs0,
  output MuxA,
  output HALT,
  output PCw
);

  wire and_1_out, and_2_out, and_3_out, and_4_out, not_1_out, scr_1_br, scr_1_jmp, scr_1_out_20, scr_1_pcw;
  wire [4:0] car_1_output, id_1_o0, multiplexer_1_out, scr_1_ad0;
  wire [17:0] rom_1_data, scr_1_hlt;

  ID id_1 (
    .I3(OPcode[3]), .O4(id_1_o0[4]), .I2(OPcode[2]), .O3(id_1_o0[3]), .I1(OPcode[1]), .I0(OPcode[0]),
    .O2(id_1_o0[2]), .O1(id_1_o0[1]), .O0(id_1_o0[0]));
  and and_1 (and_1_out, 1'b1, scr_1_br);
  Multiplexer #(.width(5), .enable("false")) multiplexer_1 (
    .in0(id_1_o0), .in1(scr_1_ad0), .out(multiplexer_1_out), .sel(scr_1_out_20));
  CAR car_1 (.\input (multiplexer_1_out), .clear(clear), .\output (car_1_output), .clk(clock), .Write(and_1_out));
  and and_2 (and_2_out, OPcode[3], OPcode[1], scr_1_jmp, Neg_flag);
  SCR scr_1 (
    .Din(rom_1_data), .clock(not_1_out), .clear(clear), .MEMw(MEMw), .MEMr(MEMr), .PCw(scr_1_pcw), .IRw(IRw),
    .MuxA(MuxA), .MuxB(MuxB), .ACCw(ACCw), .ACCr(ACCr), .ALUs1(ALUs1), .ALUs0(ALUs0), .BR(scr_1_br),
    .out_20(scr_1_out_20), .AD4(scr_1_ad0[4]), .AD3(scr_1_ad0[3]), .AD2(scr_1_ad0[2]), .AD1(scr_1_ad0[1]),
    .AD0(scr_1_ad0[0]), .HLT(scr_1_hlt), .JMP(scr_1_jmp));
  ROM #(.addrWidth(5), .dataWidth(18), .Select("high"), .simpleMode("false")) rom_1 (
    .addr(car_1_output), .data(rom_1_data));
  and and_3 (and_3_out, OPcode[2], OPcode[1], scr_1_jmp, zero_flag);
  not not_1 (not_1_out, clock);
  or or_1 (PCw, and_3_out, and_2_out, scr_1_pcw, and_4_out);
  and and_4 (and_4_out, OPcode[3], OPcode[0], scr_1_jmp, pos_flag);
  and and_5 (HALT, scr_1_hlt[16], scr_1_hlt[15], scr_1_hlt[14], scr_1_hlt[13], scr_1_hlt[12], scr_1_hlt[11], scr_1_hlt[10], scr_1_hlt[9], scr_1_hlt[8], scr_1_hlt[7], scr_1_hlt[6], scr_1_hlt[5], scr_1_hlt[4], scr_1_hlt[3], scr_1_hlt[2], scr_1_hlt[1]);

  // Notes on the sheet:
  //   contents of rom_1 (hex, n*v repeats v):
  //   e180 40 9c60 19260 9d60 9ce0 5060 21060 1ffff
endmodule

module SCR (
  input  [17:0] Din,
  input  clock,
  input  clear,
  output [17:0] HLT,
  output JMP,
  output MEMw,
  output PCw,
  output MuxA,
  output ACCw,
  output ALUs1,
  output BR,
  output AD4,
  output AD2,
  output AD0,
  output MEMr,
  output IRw,
  output MuxB,
  output ACCr,
  output ALUs0,
  output out_20,
  output AD3,
  output AD1
);

  Register #(.width(18), .Select("low")) register_1 (
    .D(Din), .en(1'b1), .Q({HLT[17:11], ACCw, ACCr, ALUs1, ALUs0, BR, HLT[5], AD4, AD3, AD2, AD1, AD0}),
    .clk(clock), .clr(clear));

  assign {HLT[10:6], HLT[4:0]} = {ACCw, ACCr, ALUs1, ALUs0, BR, AD4, AD3, AD2, AD1, AD0};
  assign IRw = HLT[13];
  assign JMP = HLT[17];
  assign MEMr = HLT[15];
  assign MEMw = HLT[16];
  assign MuxA = HLT[12];
  assign MuxB = HLT[11];
  assign out_20 = HLT[5];
  assign PCw = HLT[14];
endmodule

module ID (
  input  I3,
  input  I2,
  input  I1,
  input  I0,
  output O4,
  output O3,
  output O2,
  output O1,
  output O0
);

  wire and_2_out, and_3_out, and_4_out, and_5_out, and_6_out, and_7_out, and_8_out, and_9_out, not_1_out,
       not_2_out, not_3_out, not_4_out, not_5_out, not_6_out, not_7_out, not_8_out, not_9_out;

  and and_1 (O3, I3, I2);
  not not_1 (not_1_out, I3);
  and and_2 (and_2_out, not_1_out, I1);
  not not_2 (not_2_out, I3);
  and and_3 (and_3_out, not_2_out, I2);
  and and_4 (and_4_out, I3, not_3_out);
  not not_3 (not_3_out, I2);
  not not_4 (not_4_out, I1);
  not not_5 (not_5_out, I3);
  and and_5 (and_5_out, not_5_out, I2);
  and and_6 (and_6_out, I3, not_6_out);
  not not_6 (not_6_out, I2);
  not not_7 (not_7_out, I2);
  and and_7 (and_7_out, not_7_out, I0);
  not not_8 (not_8_out, I3);
  and and_8 (and_8_out, not_8_out, I2, I1);
  and and_9 (and_9_out, I3, not_9_out);
  not not_9 (not_9_out, I2);
  or or_1 (O2, and_2_out, and_3_out, and_4_out);
  or or_2 (O1, not_4_out, and_5_out, and_6_out);
  or or_3 (O0, and_7_out, and_8_out, and_9_out);

  assign O4 = 1'b0;
endmodule

module register_12bits (
  input  [11:0] Data_in,
  input  Clock,
  input  Write,
  input  clear,
  input  Read,
  output [11:0] Data_out,
  output [11:0] Data_stored
);

  D_Flip_Flop #(.Pre_Clr_Positions("LEGACY"), .enable("true")) d_ff_1 (
    .clk(Clock), .D(Data_in[0]), .Q(Data_stored[0]), .en(Write), .reset(clear));  // open: Qn, preset
  D_Flip_Flop #(.Pre_Clr_Positions("LEGACY"), .enable("true")) d_ff_2 (
    .clk(Clock), .D(Data_in[1]), .Q(Data_stored[1]), .en(Write), .reset(clear));  // open: Qn, preset
  D_Flip_Flop #(.Pre_Clr_Positions("LEGACY"), .enable("true")) d_ff_3 (
    .clk(Clock), .D(Data_in[2]), .Q(Data_stored[2]), .en(Write), .reset(clear));  // open: Qn, preset
  D_Flip_Flop #(.Pre_Clr_Positions("LEGACY"), .enable("true")) d_ff_4 (
    .clk(Clock), .D(Data_in[3]), .Q(Data_stored[3]), .en(Write), .reset(clear));  // open: Qn, preset
  D_Flip_Flop #(.Pre_Clr_Positions("LEGACY"), .enable("true")) d_ff_5 (
    .clk(Clock), .D(Data_in[4]), .Q(Data_stored[4]), .en(Write), .reset(clear));  // open: Qn, preset
  D_Flip_Flop #(.Pre_Clr_Positions("LEGACY"), .enable("true")) d_ff_6 (
    .clk(Clock), .D(Data_in[5]), .Q(Data_stored[5]), .en(Write), .reset(clear));  // open: Qn, preset
  assign Data_out = Read ? Data_stored : 12'bz;  // Controlled_Buffer controlled_buffer_1
  D_Flip_Flop #(.Pre_Clr_Positions("LEGACY"), .enable("true")) d_ff_7 (
    .clk(Clock), .D(Data_in[6]), .Q(Data_stored[6]), .en(Write), .reset(clear));  // open: Qn, preset
  D_Flip_Flop #(.Pre_Clr_Positions("LEGACY"), .enable("true")) d_ff_8 (
    .clk(Clock), .D(Data_in[7]), .Q(Data_stored[7]), .en(Write), .reset(clear));  // open: Qn, preset
  D_Flip_Flop #(.Pre_Clr_Positions("LEGACY"), .enable("true")) d_ff_9 (
    .clk(Clock), .D(Data_in[8]), .Q(Data_stored[8]), .en(Write), .reset(clear));  // open: Qn, preset
  D_Flip_Flop #(.Pre_Clr_Positions("LEGACY"), .enable("true")) d_ff_10 (
    .clk(Clock), .D(Data_in[9]), .Q(Data_stored[9]), .en(Write), .reset(clear));  // open: Qn, preset
  D_Flip_Flop #(.Pre_Clr_Positions("LEGACY"), .enable("true")) d_ff_11 (
    .clk(Clock), .D(Data_in[10]), .Q(Data_stored[10]), .en(Write), .reset(clear));  // open: Qn, preset
  D_Flip_Flop #(.Pre_Clr_Positions("LEGACY"), .enable("true")) d_ff_12 (
    .clk(Clock), .D(Data_in[11]), .Q(Data_stored[11]), .en(Write), .reset(clear));  // open: Qn, preset
endmodule

module register_16bits (
  input  W,
  input  [15:0] Din,
  input  OE,
  input  Clock,
  input  Clear,
  output [15:0] Dout,
  output [15:0] debug
);

  Register #(.width(16), .Select("low")) register_1 (.D(Din), .en(W), .Q(debug), .clk(Clock), .clr(Clear));
  assign Dout = OE ? debug : 16'bz;  // Controlled_Buffer controlled_buffer_1
endmodule

module OR (
  input  ORw,
  input  Clock,
  input  [15:0] Din,
  input  clear,
  output [15:0] Dout
);

  register_16bits register_16bits_1 (
    .Din(Din), .Dout(Dout), .W(ORw), .Clock(Clock), .Clear(clear), .OE(1'b1));  // open: debug
endmodule
